# Fritzing sketch rx (saved by Fritzing 0.8.7b)

parts:
  LCD = 20x4 LCD display [part_number=2004A]
  Microcontroller = Adafruit Feather 32u4 RFM9xW LoRa [part_number="32u4 with LoRa Radio (433Mhz)"]
  Pot = POT [package=pot_alpha_rv16af-20]
  ANT1 = Antenna

nets:
  VSS: LCD.Vss, LCD.K_-, Microcontroller.GND, Pot.A
  VDD: LCD.Vdd, LCD.A_+, Microcontroller.+3V3, Pot.E
  N1: LCD.Vo, Pot.S
  N2: LCD.RS, Microcontroller.A0
  N3: LCD.E, Microcontroller.A1
  N4: LCD.DB4, Microcontroller.A2
  N5: LCD.DB5, Microcontroller.A3
  N6: LCD.DB6, Microcontroller.A4
  N7: LCD.DB7, Microcontroller.A5
  N8: Microcontroller.ANT, ANT1.antenna_lead

custom parts:
  20x4 LCD display: 20x4 character display. CHECK LED POLARITY BEFORE CONNECTING POWER Some versions of the dispaly have the polarity of the LED pins "A" and "K" reversed.
  Adafruit Feather 32u4 RFM9xW LoRa: This is the Adafruit Feather 32u4 LoRa Radio (RFM9x) - our take on an microcontroller with a "Long Range (LoRa)" packet radio transceiver with built in USB and battery charging. Its an Adafruit Feather 32u4 with a 868/915 MHz radio module cooked in! Great for making wireless networks that can go further than 2.4GHz 802.15.4 and similar, are more flexible than Bluetooth LE and without the high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
