# Fritzing sketch tx (saved by Fritzing 0.9.4)
circuit board: 10cm x 2.5cm

parts:
  433Mhz_Ant = Antenna
  GPS = u-blox NEO-6M GPS Breakout
  Wx_Senor = Humidity and Temperature Sensor RHT03
  Microcontroller = Adafruit Feather 32u4 RFM9xW LoRa [part_number="32u4 with LoRa Radio (433Mhz)"]

nets:
  N1: 433Mhz_Ant.antenna_lead, Microcontroller.ANT
  GND: GPS.GND, Wx_Senor.GND_1, Microcontroller.GND
  VCC: GPS.VCC, Wx_Senor.Vcc, Microcontroller.+3V3
  N2: GPS.TXD, Microcontroller.11
  N3: GPS.RXD, Microcontroller.10
  N4: Wx_Senor.Data-signal, Microcontroller.A0

custom parts:
  Adafruit Feather 32u4 RFM9xW LoRa: This is the Adafruit Feather 32u4 LoRa Radio (RFM9x) - our take on an microcontroller with a "Long Range (LoRa)" packet radio transceiver with built in USB and battery charging. Its an Adafruit Feather 32u4 with a 868/915 MHz radio module cooked in! Great for making wireless networks that can go further than 2.4GHz 802.15.4 and similar, are more flexible than Bluetooth LE and without the high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
